# Fritzing sketch pin (saved by Fritzing 0.9.3b)

parts:
  Часть1 = Arduino Nano (Rev3.0)
  HC-SR04_Sensor_1 = HC-SR04 Ultrasonic Distance Sensor
  J1 = Basic Servo
  J2 = Basic Servo
  R1 = Resistor [tolerance=±5% resistance=150 package=THT]
  LD2 = LD

nets:
  GND: Часть1.GND, J1.gnd, J2.gnd
  N1: Часть1.D5, R1.Pin_1
  N2: Часть1.D7, J2.pulse
  N3: Часть1.D9, J1.pulse
  N4: Часть1.D11/MOSI, HC-SR04_Sensor_1.ECHO
  N5: Часть1.D12/MISO, HC-SR04_Sensor_1.TRIG
  VCC: Часть1.5V, HC-SR04_Sensor_1.VCC, J1.vcc, J2.vcc
  N6: HC-SR04_Sensor_1.GND, LD2.cathode

custom parts:
  LD: A Generic Red Dot Laser Diode Module (~5mW)
